# Fritzing sketch FSR_PressureSensorTest (saved by Fritzing 1.0.1rc)
breadboards: 1

parts:
  A1 = Particle - Photon2
  U1 = WS2812 RGB LED strip
  J1 = Basic Force Sensing Resistor (FSR) [package=THT]
  R1 = Resistor [tolerance=±5% power=0.25W resistance=220 package=THT]

nets:
  3.3V: A1.Pin_2, J1.pin_1
  GND: A1.Pin_4, U1.GND, R1.Pin_1
  N1: A1.Pin_5, J1.pin_0, R1.Pin_0
  N2: A1.Pin_19, U1.DIN
  5V: A1.Pin_26, U1.VCC

custom parts:
  Particle - Photon2: The Photon 2 is a microcontroller and Wi-Fi networking developed by particle. Features: 802.11a/b/g/n Wi-Fi, 2.4 GHz and 5 GHz Integrated PCB antenna Integrated U.FL connector for external antenna Integrated RF switch BLE 5 using same antenna as Wi-Fi Realtek RTL8721DM MCU ARM Cortex M33 CPU, 200 MHz 2048 KB (2 MB) user application maximum size 3072 KB (3 MB) of RAM available to user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
  WS2812 RGB LED strip: WS2812 strip
